// Logisim project RSC.circ as structural Verilog: 9 circuits, main circuit Arith_U
// AU
module Arith_U (
  input  [31:0] A_32_bit_in,
  input  [31:0] B_32_bit_in,
  input  S1,
  input  S0,
  output [31:0] AU_out
);

  wire and_2_out, nor_1_out, or_1_out;
  wire [31:0] adder_1_out, and_1_out, multiplexer_1_out, not_1_out, not_2_out;

  assign and_1_out = A_32_bit_in & not_1_out;  // AND_Gate and_1, 32 bits wide
  assign not_1_out = ~A_32_bit_in;  // NOT_Gate not_1, 32 bits wide
  assign not_2_out = ~B_32_bit_in;  // NOT_Gate not_2, 32 bits wide
  Multiplexer #(.select(2), .width(32), .enable("false")) multiplexer_1 (
    .in0(not_2_out), .in1(B_32_bit_in), .in2(and_1_out), .out(multiplexer_1_out), .sel({S1, S0}));  // open: in3
  nor nor_1 (nor_1_out, S1, S0);
  Adder #(.width(32)) adder_1 (
    .a(A_32_bit_in), .b(multiplexer_1_out), .out(adder_1_out), .cin(or_1_out));  // open: cout
  or or_1 (or_1_out, S1, nor_1_out);
  and and_2 (and_2_out, S1, S0);
  Multiplexer #(.width(32), .enable("false")) multiplexer_2 (
    .in0(adder_1_out), .in1(B_32_bit_in), .out(AU_out), .sel(and_2_out));

  // Notes on the sheet:
  //   Bryce Ault
  //   Arith_Unit
endmodule

// LU
module Logic_U (
  input  [31:0] A,
  input  [31:0] B,
  input  S1,
  input  S0,
  output [31:0] Logic_Out
);

  wire [31:0] and_1_out, not_1_out, or_1_out, shifter_1_out;

  assign or_1_out = A | B;  // OR_Gate or_1, 32 bits wide
  assign not_1_out = ~A;  // NOT_Gate not_1, 32 bits wide
  assign and_1_out = A & B;  // AND_Gate and_1, 32 bits wide
  Shifter #(.width(32), .shift("ar")) shifter_1 (.in(A), .\dist (5'b00001), .out(shifter_1_out));
  Multiplexer #(.select(2), .width(32), .enable("false")) multiplexer_1 (
    .in0(and_1_out), .in1(or_1_out), .in2(shifter_1_out), .in3(not_1_out), .out(Logic_Out), .sel({S1, S0}));

  // Notes on the sheet:
  //   Bryce Ault
  //   Logic_Unit
endmodule

module ALU (
  input  [31:0] A,
  input  [31:0] B,
  input  S2,
  input  S1,
  input  S0,
  output [31:0] ALU_Out
);

  wire [31:0] arith_u_1_au_out, logic_u_1_logic_out;

  Arith_U arith_u_1 (.A_32_bit_in(A), .B_32_bit_in(B), .S1(S1), .S0(S0), .AU_out(arith_u_1_au_out));
  Logic_U logic_u_1 (.A(A), .B(B), .S1(S1), .S0(S0), .Logic_Out(logic_u_1_logic_out));
  Multiplexer #(.width(32), .enable("false")) multiplexer_1 (
    .in0(arith_u_1_au_out), .in1(logic_u_1_logic_out), .out(ALU_Out), .sel(S2));
endmodule

module SC (
  input  Clock,
  input  Clear,
  output [2:0] SEQ_Out
);

  wire not_1_out;
  wire [2:0] adder_1_out;

  Adder #(.width(3)) adder_1 (.a(3'b001), .b(SEQ_Out), .out(adder_1_out));  // open: cin, cout
  Register #(.width(3)) register_1 (.D(adder_1_out), .en(not_1_out), .Q(SEQ_Out), .clk(Clock), .clr(Clear));
  not not_1 (not_1_out, Clear);

  // Notes on the sheet:
  //   Bryce Ault
  //   cla 7
  //   SC
endmodule

module RSC (
);

  wire ACC_BUS, AR_LD, control_1_acc_clr, control_1_acc_ld, control_1_dr_ld, control_1_ir_ld,
       control_1_outr_ld, control_1_pc_bus, control_1_pc_inc, control_1_pc_ld, control_1_r_ld,
       control_1_ram_en, control_1_ram_r_prime_w, control_1_z_ld, DR_BUS, Primary_Clock_out, R_BUS,
       z_reg_1_z_out;
  wire [2:0] control_1_alu_s;
  wire [3:0] outr_1_data_out, outr_1_data_out_2, outr_1_data_out_3, outr_1_data_out_4, outr_1_data_out_5,
       outr_1_data_out_6, outr_1_data_out_7, outr_1_data_out_8;
  wire [31:0] acc_1_data_out, alu_1_alu_out, ar_1_data_out, dr_1_data_out, ir_1_data_out, r_1_bus_out;

  Clock Primary_Clock (.out(Primary_Clock_out));
  Hex_Digit_Display hex_digit_display_1 (.value(outr_1_data_out_8));  // open: dp
  R r_1 (
    .Bus(R_BUS), .Data_In(r_1_bus_out), .Load(control_1_r_ld), .Clock(Primary_Clock_out),
    .Bus_Out(r_1_bus_out));  // open: Data_Out
  Hex_Digit_Display hex_digit_display_2 (.value(outr_1_data_out_7));  // open: dp
  AR ar_1 (.Data_In(r_1_bus_out), .Load(AR_LD), .Clock(Primary_Clock_out), .Data_Out(ar_1_data_out));
  ALU alu_1 (
    .A(acc_1_data_out), .B(r_1_bus_out), .S2(control_1_alu_s[2]), .S1(control_1_alu_s[1]),
    .S0(control_1_alu_s[0]), .ALU_Out(alu_1_alu_out));
  Hex_Digit_Display hex_digit_display_3 (.value(outr_1_data_out_6));  // open: dp
  Hex_Digit_Display hex_digit_display_4 (.value(outr_1_data_out_5));  // open: dp
  DR dr_1 (
    .Bus(DR_BUS), .Data_In(r_1_bus_out), .Load(control_1_dr_ld), .Clock(Primary_Clock_out),
    .Bus_Out(r_1_bus_out), .Data_Out(dr_1_data_out));
  Hex_Digit_Display hex_digit_display_5 (.value(outr_1_data_out_4));  // open: dp
  Hex_Digit_Display hex_digit_display_6 (.value(outr_1_data_out_3));  // open: dp
  ACC acc_1 (
    .Bus(ACC_BUS), .Data_In(alu_1_alu_out), .Load(control_1_acc_ld), .Clock(Primary_Clock_out),
    .Clear(control_1_acc_clr), .Bus_Out(r_1_bus_out), .Data_Out(acc_1_data_out));
  Hex_Digit_Display hex_digit_display_7 (.value(outr_1_data_out));  // open: dp
  Hex_Digit_Display hex_digit_display_8 (.value(outr_1_data_out_2));  // open: dp
  RAM #(.addrWidth(16), .dataWidth(32)) ram_1 (
    .addr(ar_1_data_out[15:0]), .data(r_1_bus_out), .sel(control_1_ram_en), .clk(Primary_Clock_out),
    .ld(control_1_ram_r_prime_w), .clr(1'b0));
  PC pc_1 (
    .Bus(control_1_pc_bus), .Data_In(r_1_bus_out), .Count(control_1_pc_inc), .Load(control_1_pc_ld),
    .Clock(Primary_Clock_out), .Bus_Out(r_1_bus_out));  // open: Data_Out
  OUTR outr_1 (
    .Data_In(r_1_bus_out), .Load(control_1_outr_ld), .Clock(Primary_Clock_out),
    .Data_Out({outr_1_data_out_8, outr_1_data_out_7, outr_1_data_out_6, outr_1_data_out_5, outr_1_data_out_4, outr_1_data_out_3, outr_1_data_out_2, outr_1_data_out}));
  IR ir_1 (.Data_In(dr_1_data_out), .Load(control_1_ir_ld), .Clock(Primary_Clock_out), .Data_Out(ir_1_data_out));
  Z_Reg z_reg_1 (.ACC_In(acc_1_data_out), .Clock(Primary_Clock_out), .Load(control_1_z_ld), .Z_Out(z_reg_1_z_out));
  Control control_1 (
    .RAM_R_prime_W(control_1_ram_r_prime_w), .RAM_EN(control_1_ram_en), .AR_LD(AR_LD),
    .PC_BUS(control_1_pc_bus), .PC_INC(control_1_pc_inc), .PC_LD(control_1_pc_ld), .DR_BUS(DR_BUS),
    .DR_LD(control_1_dr_ld), .R_BUS(R_BUS), .R_LD(control_1_r_ld), .ACC_BUS(ACC_BUS),
    .ACC_CLR(control_1_acc_clr), .ACC_LD(control_1_acc_ld), .ALU_S(control_1_alu_s),
    .OUTR_LD(control_1_outr_ld), .Z_LD(control_1_z_ld), .IR_LD(control_1_ir_ld), .Clock(Primary_Clock_out),
    .Z_In(z_reg_1_z_out), .IR_in(ir_1_data_out));  // open: T, D

  // Notes on the sheet:
  //   Bryce Ault
  //   Ola 9
  //   RSC
endmodule

module Decoder (
  input  [31:0] IR_In,
  output [15:0] D_Out,
  output [3:0] Debug_Instruction
);

  wire or_1_out;
  wire [3:0] or_2_out;
  wire [15:0] decoder_1_out0;

  Multiplexer #(.width(16), .enable("false")) multiplexer_1 (
    .in0(decoder_1_out0), .in1({16{1'b0}}), .out(D_Out), .sel(or_1_out));
  or or_1 (or_1_out, or_2_out[3], or_2_out[2], or_2_out[1], or_2_out[0]);
  Decoder_part #(.select(4), .enable("false")) decoder_1 (
    .out0(decoder_1_out0[0]), .out1(decoder_1_out0[1]), .out2(decoder_1_out0[2]), .out3(decoder_1_out0[3]),
    .out4(decoder_1_out0[4]), .out5(decoder_1_out0[5]), .out6(decoder_1_out0[6]), .out7(decoder_1_out0[7]),
    .out8(decoder_1_out0[8]), .out9(decoder_1_out0[9]), .out10(decoder_1_out0[10]),
    .out11(decoder_1_out0[11]), .out12(decoder_1_out0[12]), .out13(decoder_1_out0[13]),
    .out14(decoder_1_out0[14]), .out15(decoder_1_out0[15]), .sel(IR_In[3:0]));
  assign or_2_out = IR_In[7:4] | IR_In[11:8] | IR_In[15:12] | IR_In[19:16] | IR_In[23:20] | IR_In[27:24] | IR_In[31:28];  // OR_Gate or_2, 4 bits wide

  assign Debug_Instruction = IR_In[3:0];

  // Notes on the sheet:
  //   Bryce Ault
  //   cla 8
  //   Decoder
endmodule

module Timer (
  input  Clear,
  input  Clock,
  input  Stop,
  output [7:0] T_Out
);

  wire [2:0] sc_1_seq_out;
  wire [7:0] decoder_1_out0;

  Multiplexer #(.width(8), .enable("false")) multiplexer_1 (
    .in0(decoder_1_out0), .in1({8{1'b0}}), .out(T_Out), .sel(Stop));
  Decoder_part #(.select(3), .enable("false")) decoder_1 (
    .out0(decoder_1_out0[0]), .out1(decoder_1_out0[1]), .out2(decoder_1_out0[2]), .out3(decoder_1_out0[3]),
    .out4(decoder_1_out0[4]), .out5(decoder_1_out0[5]), .out6(decoder_1_out0[6]), .out7(decoder_1_out0[7]),
    .sel(sc_1_seq_out));
  SC sc_1 (.Clock(Clock), .Clear(Clear), .SEQ_Out(sc_1_seq_out));

  // Notes on the sheet:
  //   Bryce Ault
  //   cla 8
  //   Timer
endmodule

// Z
module Z_Reg (
  input  Clock,
  input  [31:0] ACC_In,
  input  Load,
  output Z_Out
);

  wire not_1_out, or_1_out;

  or or_1 (or_1_out, ACC_In[31], ACC_In[30], ACC_In[29], ACC_In[28], ACC_In[27], ACC_In[26], ACC_In[25], ACC_In[24], ACC_In[23], ACC_In[22], ACC_In[21], ACC_In[20], ACC_In[19], ACC_In[18], ACC_In[17], ACC_In[16], ACC_In[15], ACC_In[14], ACC_In[13], ACC_In[12], ACC_In[11], ACC_In[10], ACC_In[8], ACC_In[7], ACC_In[6], ACC_In[5], ACC_In[4], ACC_In[3], ACC_In[2], ACC_In[1], ACC_In[0], ACC_In[9]);
  not not_1 (not_1_out, or_1_out);
  _1bit_reg u_1bit_reg_1 (.Data(not_1_out), .Clock(Clock), .Load(Load), .Data_out(Z_Out));  // open: Clear
endmodule

// CU
module Control (
  input  Clock,
  input  [31:0] IR_in,
  input  Z_In,
  output IR_LD,
  output [7:0] T,
  output RAM_R_prime_W,
  output RAM_EN,
  output [3:0] D,
  output AR_LD,
  output PC_BUS,
  output PC_INC,
  output PC_LD,
  output DR_BUS,
  output DR_LD,
  output R_BUS,
  output R_LD,
  output ACC_BUS,
  output ACC_CLR,
  output ACC_LD,
  output [2:0] ALU_S,
  output OUTR_LD,
  output Z_LD
);

  wire n1bit_reg_1_data_out, s_ld_1_s_ld, sc_clr_1_sc_clr;
  wire [7:0] timer_1_t_out;
  wire [15:0] decoder_1_d_out;

  IR_LD ir_ld_1 (.t2(timer_1_t_out[2]), .clock(Clock), .IR_LD(IR_LD));
  RAM_RW ram_rw_1 (
    .t1(timer_1_t_out[1]), .t3(timer_1_t_out[3]), .t5(timer_1_t_out[5]), .d1(decoder_1_d_out[1]),
    .d2(decoder_1_d_out[2]), .d5(decoder_1_d_out[5]), .d6(decoder_1_d_out[6]), .z(Z_In),
    .RAM_RW(RAM_R_prime_W));
  RAM_EN ram_en_1 (
    .t1(timer_1_t_out[1]), .t3(timer_1_t_out[3]), .t5(timer_1_t_out[5]), .t6(timer_1_t_out[6]),
    .d1(decoder_1_d_out[1]), .d2(decoder_1_d_out[2]), .d5(decoder_1_d_out[5]), .d6(decoder_1_d_out[6]),
    .z(Z_In), .RAM_EN(RAM_EN));
  AR_LD ar_ld_1 (
    .t0(timer_1_t_out[0]), .t2(timer_1_t_out[2]), .t4(timer_1_t_out[4]), .clock(Clock),
    .d1(decoder_1_d_out[1]), .d2(decoder_1_d_out[2]), .AR_LD(AR_LD));
  PC_BUS pc_bus_1 (.t0(timer_1_t_out[0]), .t2(timer_1_t_out[2]), .PC_BUS(PC_BUS));
  PC_INC pc_inc_1 (
    .t1(timer_1_t_out[1]), .t3(timer_1_t_out[3]), .clock(Clock), .d1(decoder_1_d_out[1]),
    .d2(decoder_1_d_out[2]), .d6(decoder_1_d_out[6]), .z(Z_In), .PC_INC(PC_INC));
  PC_LD pc_ld_1 (
    .t4(timer_1_t_out[4]), .clock(Clock), .d5(decoder_1_d_out[5]), .d6(decoder_1_d_out[6]), .z(Z_In),
    .PC_LD(PC_LD));
  DR_BUS dr_bus_1 (
    .t4(timer_1_t_out[4]), .t6(timer_1_t_out[6]), .d1(decoder_1_d_out[1]), .d2(decoder_1_d_out[2]),
    .d5(decoder_1_d_out[5]), .d6(decoder_1_d_out[6]), .z(Z_In), .DR_BUS(DR_BUS));
  DR_LD dr_ld_1 (
    .t1(timer_1_t_out[1]), .t3(timer_1_t_out[3]), .t5(timer_1_t_out[5]), .clock(Clock),
    .d1(decoder_1_d_out[1]), .d2(decoder_1_d_out[2]), .d5(decoder_1_d_out[5]), .d6(decoder_1_d_out[6]),
    .z(Z_In), .DR_LD(DR_LD));
  R_BUS r_bus_1 (
    .t3(timer_1_t_out[3]), .d4(decoder_1_d_out[4]), .d8(decoder_1_d_out[8]), .d9(decoder_1_d_out[9]),
    .d12(decoder_1_d_out[12]), .d13(decoder_1_d_out[13]), .R_BUS(R_BUS));
  R_LD r_ld_1 (.t3(timer_1_t_out[3]), .clock(Clock), .d3(decoder_1_d_out[3]), .R_LD(R_LD));
  ACC_BUS acc_bus_1 (
    .t3(timer_1_t_out[3]), .t5(timer_1_t_out[5]), .d2(decoder_1_d_out[2]), .d3(decoder_1_d_out[3]),
    .d7(decoder_1_d_out[7]), .ACC_BUS(ACC_BUS));
  ACC_CLR acc_clr_1 (.t3(timer_1_t_out[3]), .d11(decoder_1_d_out[11]), .ACC_CLR(ACC_CLR));
  ACC_LD acc_ld_1 (
    .t3(timer_1_t_out[3]), .t6(timer_1_t_out[6]), .clock(Clock), .d1(decoder_1_d_out[1]),
    .d4(decoder_1_d_out[4]), .d8(decoder_1_d_out[8]), .d9(decoder_1_d_out[9]), .d10(decoder_1_d_out[10]),
    .d12(decoder_1_d_out[12]), .d13(decoder_1_d_out[13]), .d14(decoder_1_d_out[14]),
    .d15(decoder_1_d_out[15]), .ACC_LD(ACC_LD));
  ALU_SEL alu_sel_1 (
    .d1(decoder_1_d_out[1]), .d4(decoder_1_d_out[4]), .d9(decoder_1_d_out[9]), .d10(decoder_1_d_out[10]),
    .d12(decoder_1_d_out[12]), .d13(decoder_1_d_out[13]), .d14(decoder_1_d_out[14]),
    .d15(decoder_1_d_out[15]), .s2(ALU_S[2]), .s1(ALU_S[1]), .s0(ALU_S[0]));
  OUTR_LD outr_ld_1 (.t3(timer_1_t_out[3]), .clock(Clock), .d7(decoder_1_d_out[7]), .OUTR_LD(OUTR_LD));
  Z_LD z_ld_1 (.out_1(Z_LD));
  S_LD s_ld_1 (.t3(timer_1_t_out[3]), .clock(Clock), .d0(decoder_1_d_out[0]), .S_LD(s_ld_1_s_ld));
  SC_CLR sc_clr_1 (
    .t4(timer_1_t_out[4]), .t5(timer_1_t_out[5]), .t7(timer_1_t_out[7]), .d1(decoder_1_d_out[1]),
    .d2(decoder_1_d_out[2]), .d5(decoder_1_d_out[5]), .d6(decoder_1_d_out[6]), .z(Z_In),
    .SC_CLR(sc_clr_1_sc_clr));
  Timer timer_1 (.T_Out(timer_1_t_out), .Clear(sc_clr_1_sc_clr), .Clock(Clock), .Stop(n1bit_reg_1_data_out));
  _1bit_reg u_1bit_reg_1 (
    .Data(1'b1), .Clock(Clock), .Load(s_ld_1_s_ld), .Clear(1'b0), .Data_out(n1bit_reg_1_data_out));
  Decoder decoder_1 (.D_Out(decoder_1_d_out), .IR_In(IR_in));  // open: Debug_Instruction

  // Notes on the sheet:
  //   Bryce Ault
  //   OLA 7
  //   Control
endmodule
