// Logisim project custom_reg.circ as structural Verilog: 11 circuits, main circuit Register
module Register (
  input  [31:0] Data_In,
  input  Load,
  input  Clock,
  output [31:0] Data_Out
);

  Register_part #(.width(32)) register_1 (.D(Data_In), .en(Load), .Q(Data_Out), .clk(Clock));  // open: clr

  // Notes on the sheet:
  //   Bryce Ault
  //   OLA 5
  //   Register
endmodule

module BusRegister (
  input  Bus,
  input  [31:0] Data_In,
  input  Load,
  input  Clock,
  output [31:0] Bus_Out,
  output [31:0] Data_Out
);

  Register_part #(.width(32)) register_1 (.D(Data_In), .en(Load), .Q(Data_Out), .clk(Clock));  // open: clr
  assign Bus_Out = Bus ? Data_Out : 32'bz;  // Controlled_Buffer controlled_buffer_1

  // Notes on the sheet:
  //   Bryce Ault
  //   OLA 5
  //   BusRegister
endmodule

module ClearRegister (
  input  Bus,
  input  [31:0] Data_In,
  input  Load,
  input  Clock,
  input  Clear,
  output [31:0] Bus_Out,
  output [31:0] Data_Out
);

  Register_part #(.width(32)) register_1 (.D(Data_In), .en(Load), .Q(Data_Out), .clk(Clock), .clr(Clear));
  assign Bus_Out = Bus ? Data_Out : 32'bz;  // Controlled_Buffer controlled_buffer_1

  // Notes on the sheet:
  //   Bryce Ault
  //   OLA 5
  //   ClearRegister
endmodule

module CountRegister (
  input  Bus,
  input  [31:0] Data_In,
  input  Load,
  input  Clock,
  input  Count,
  output [31:0] Bus_Out,
  output [31:0] Data_Out
);

  wire or_1_out;
  wire [31:0] adder_1_out, multiplexer_1_out;

  Multiplexer #(.width(32), .enable("false")) multiplexer_1 (
    .in0(Data_In), .in1(adder_1_out), .out(multiplexer_1_out), .sel(Count));
  Adder #(.width(32)) adder_1 (.a(32'h1), .b(Data_Out), .out(adder_1_out));  // open: cin, cout
  or or_1 (or_1_out, Count, Load);
  Register_part #(.width(32)) register_1 (
    .D(multiplexer_1_out), .en(or_1_out), .Q(Data_Out), .clk(Clock));  // open: clr
  assign Bus_Out = Bus ? Data_Out : 32'bz;  // Controlled_Buffer controlled_buffer_1

  // Notes on the sheet:
  //   Bryce Ault
  //   OLA 5
  //   CountRegister
endmodule

module ACC (
  input  Bus,
  input  [31:0] Data_In,
  input  Load,
  input  Clock,
  input  Clear,
  output [31:0] Bus_Out,
  output [31:0] Data_Out
);

  ClearRegister clearregister_1 (
    .Bus(Bus), .Data_In(Data_In), .Load(Load), .Clock(Clock), .Clear(Clear), .Bus_Out(Bus_Out),
    .Data_Out(Data_Out));

  // Notes on the sheet:
  //   Bryce Ault
  //   OLA 5
  //   ACC
endmodule

module AR (
  input  [31:0] Data_In,
  input  Load,
  input  Clock,
  output [31:0] Data_Out
);

  Register register_1 (.Data_In(Data_In), .Load(Load), .Clock(Clock), .Data_Out(Data_Out));

  // Notes on the sheet:
  //   Bryce Ault
  //   OLA 5
  //   AR
endmodule

module DR (
  input  Bus,
  input  [31:0] Data_In,
  input  Load,
  input  Clock,
  output [31:0] Bus_Out,
  output [31:0] Data_Out
);

  BusRegister busregister_1 (
    .Bus(Bus), .Data_In(Data_In), .Load(Load), .Clock(Clock), .Bus_Out(Bus_Out), .Data_Out(Data_Out));

  // Notes on the sheet:
  //   Bryce Ault
  //   OLA 5
  //   DR
endmodule

module IR (
  input  [31:0] Data_In,
  input  Load,
  input  Clock,
  output [31:0] Data_Out
);

  Register register_1 (.Data_In(Data_In), .Load(Load), .Clock(Clock), .Data_Out(Data_Out));

  // Notes on the sheet:
  //   Bryce Ault
  //   OLA 5
  //   IR
endmodule

module OUTR (
  input  [31:0] Data_In,
  input  Load,
  input  Clock,
  output [31:0] Data_Out
);

  Register register_1 (.Data_In(Data_In), .Load(Load), .Clock(Clock), .Data_Out(Data_Out));

  // Notes on the sheet:
  //   Bryce Ault
  //   OLA 5
  //   OUTR
endmodule

module PC (
  input  Bus,
  input  [31:0] Data_In,
  input  Count,
  input  Load,
  input  Clock,
  output [31:0] Bus_Out,
  output [31:0] Data_Out
);

  CountRegister countregister_1 (
    .Bus(Bus), .Data_In(Data_In), .Count(Count), .Load(Load), .Clock(Clock), .Bus_Out(Bus_Out),
    .Data_Out(Data_Out));

  // Notes on the sheet:
  //   Bryce Ault
  //   OLA 5
  //   PC
endmodule

module R (
  input  Bus,
  input  [31:0] Data_In,
  input  Load,
  input  Clock,
  output [31:0] Bus_Out,
  output [31:0] Data_Out
);

  BusRegister busregister_1 (
    .Bus(Bus), .Data_In(Data_In), .Load(Load), .Clock(Clock), .Bus_Out(Bus_Out), .Data_Out(Data_Out));

  // Notes on the sheet:
  //   Bryce Ault
  //   OLA 5
  //   R
endmodule
